# Fritzing sketch photocell (saved by Fritzing 0.9.2b)
breadboards: 1

parts:
  Raspberry_Pi1 = Raspberry Pi 2
  R1 = Photocell (LDR) [package=THT]
  C1 = Capacitor [package=cap-pth-small-kit]
  Power_plug1 = Power plug
  D1 = Diode [package=diode-hv]
  NEOPIXEL1 = Neopixel Strip -- Black (60/m)

nets:
  N1: Raspberry_Pi1.3v3, R1.pin_0
  N2: Raspberry_Pi1.GPIO12, NEOPIXEL1.+5V
  N3: Raspberry_Pi1.GPIO18, R1.pin_1, C1.1
  N4: Raspberry_Pi1.GND, C1.2
  GND: Power_plug1.GND, NEOPIXEL1.GND
  N5: Power_plug1.VCC, D1.A
  N6: D1.C, NEOPIXEL1.DI

custom parts:
  Neopixel Strip -- Black (60/m): Neopixel Strip, Black, 60 pixels per meter.
